# Fritzing sketch schematics (saved by Fritzing 0.9.5d)

parts:
  Part1 = Arduino Uno (Rev3)
  Disp1 = LBT2088AH [part_number=LBT2088AH]
  S1 = SWITCH-MOMENTARY-2 [package=tactile_switch_smd]
  R1 = Resistor [tolerance=±5% resistance=220 package="2010 [SMD]"]

nets:
  N1: Part1.A2, Disp1.pin_5
  N2: Part1.A3, Disp1.pin_4
  N3: Part1.A4/SDA, Disp1.pin_3
  N4: Part1.A5/SCL, Disp1.pin2
  N5: Part1.D8, S1.1
  N6: Part1.GND, R1.Pin_0
  N7: Part1.D2, Disp1.pin_16
  N8: Part1.D3_PWM, Disp1.pin_15
  N9: Part1.D4, Disp1.pin_14
  N10: Part1.D5_PWM, Disp1.pin_13
  N11: Part1.D6_PWM, Disp1.pin_12
  N12: Part1.5V, S1.2
